# Fritzing sketch smart_tc_fritzing (saved by Fritzing 0.9.10b)
breadboards: 1

parts:
  HC-SR04_Sensor_1 = HC-SR04 Ultrasonic Distance Sensor
  LED1 = RGB LED - (4 legs) [package="5 mm [THT]"]
  R1 = Resistor [tolerance=±5% resistance=220 package="0402 [SMD]"]
  R2 = Resistor [tolerance=±5% resistance=220 package="0402 [SMD]"]
  R3 = Resistor [tolerance=±5% resistance=220 package="0402 [SMD]"]
  Part1 = Arduino Mega 2560 (Rev3)
  LED2 = smd LED [color="Red (633nm)" package="0805 [SMD]"]
  R4 = Resistor [tolerance=±5% resistance=220 package="0603 [SMD]"]
  S1 = TILT-SWITCH-SW-200D [package=reed_switch_plastic]
  LED3 = smd LED [color="Red (633nm)" package="0805 [SMD]"]
  R5 = Resistor [tolerance=±5% resistance=220 package="0603 [SMD]"]
  U1 = ESP8266 WiFi Module [part_number=ESP8266]
  M1_IR_object_avoidance = fc-51 [package=THT]
  LED4 = RGB LED (com. cathode, rgb) [package="5 mm [THT]"]  # not connected

nets:
  VCC: HC-SR04_Sensor_1.VCC, Part1.5V, M1_IR_object_avoidance.pin3
  N1: HC-SR04_Sensor_1.TRIG, Part1.D2_PWM
  N2: HC-SR04_Sensor_1.ECHO, Part1.D3_PWM
  GND: HC-SR04_Sensor_1.GND, LED1.common_anode, Part1.GND, LED2.cathode, S1.1, LED3.cathode, U1.GND, M1_IR_object_avoidance.pin2
  N3: LED1.red_cathode, R3.Pin_1
  N4: LED1.green_cathode, R2.Pin_1
  N5: LED1.blue_cathode, R1.Pin_1
  N6: R1.Pin_0, Part1.D4_PWM
  N7: R2.Pin_0, Part1.D6_PWM
  N8: R3.Pin_0, Part1.D5_PWM
  N9: Part1.D19/RX1, U1.TX
  N10: Part1.D18/TX1, U1.RX
  N11: Part1.D11_PWM, R4.Pin_0
  N12: Part1.D10_PWM, M1_IR_object_avoidance.pin1
  N13: Part1.D8_PWM, R5.Pin_0
  3V3: Part1.3V3, U1.3.3V
  N14: Part1.D7_PWM, S1.2
  N15: LED2.anode, R4.Pin_1
  N16: LED3.anode, R5.Pin_1

notes:
  Ultrasonic sensor Trash can
  Ir object avoidance trash can ( missing EN pin here should map to 9)
  Tilt sensor
  Ir Avoidance Trash Can ( missing EN pin in schematic )
  IR tilt trash can
  Ultrasonic sensor trash can
